# Fritzing sketch KetosensePi_0.1 (saved by Fritzing 0.9.3b)
breadboards: 1

parts:
  Part1 = Gas Sensor Breakout Board
  I2C_LCD1 = I2C LCD screen
  IC1 = DIP - 14 pins [chip_label=MCP3204-C package="DIP (Dual Inline) [THT]"]
  R1 = Resistor [tolerance=±5% resistance=10k package=THT]
  RHT1 = Humidity and Temperature Sensor RHT03
  S1 = Pushbutton [package="[THT]"]
  R2 = Resistor [tolerance=±5% resistance=10k package=THT]
  S2 = Pushbutton [package="[THT]"]
  S3 = Pushbutton [package="[THT]"]
  R3 = Resistor [tolerance=±5% resistance=10k package=THT]
  R4 = Resistor [tolerance=±5% resistance=10k package=THT]
  Part2 = Adafruit T-Cobbler Plus [part_number="Adafruit #1989 and #2028"]

nets (from the breadboard view):
  N1: Part1.A1, IC1.CH0, R1.Pin_1
  VCC: Part1.B1, Part1.H1, I2C_LCD1.VCC, Part2.+5V
  GND: Part1.GND, I2C_LCD1.GND, IC1.DGND, IC1.AGND, R1.Pin_0, RHT1.GND_2, R2.Pin_1, R3.Pin_1, R4.Pin_1, Part2.GND
  N2: I2C_LCD1.SDA, Part2.SDA
  N3: I2C_LCD1.SCL, Part2.SCL
  N4: IC1.CS/SHDN, Part2.GPIO25
  N5: IC1.D_IN, Part2.GPIO24
  N6: IC1.D_OUT, Part2.GPIO23
  N7: IC1.CLK, Part2.GPIO18
  N8: IC1.V_REF, IC1.V_DD, RHT1.Vcc, S1.Pin_3, S1.Pin_4, S2.Pin_3, S2.Pin_4, S3.Pin_3, S3.Pin_4, Part2.+3.3V_2
  N9: RHT1.Data-signal, Part2.CE0
  N10: S1.Pin_1, S1.Pin_2, R2.Pin_0, Part2.SCLK
  N11: S2.Pin_1, S2.Pin_2, R3.Pin_0, Part2.MISO
  N12: S3.Pin_1, S3.Pin_2, R4.Pin_0, Part2.MOSI

notes:
  KetoSense for RasPi 2/3
  The KetoSense is a prototype breath analyzer to detect ethanol in the breath, a proxy for ketogenesis.
  This configuration uses the TGS 822 gas sensor, Raspberry Pi 2, and various parts from the Osoyoo Raspberry Pi Starter Kit.

custom parts:
  I2C LCD screen: An I2C-based 2x16 character display included in Osoyoo Raspberry Pi kits.
  DIP - 14 pins: A DIP stand-in part for whatever IC you want. With 14 pins on a 300mil dual inline package (DIP) footprint.
  Adafruit T-Cobbler Plus: The Raspberry Pi has landed on the Maker World like a 40-GPIO pinned, quad-USB ported, credit card sized bomb of DIY joy. And while you can use most of our great Model B accessories by hooking up our downgrade cable, its probably a good time to upgrade your set up and accessorize using all of the 40 pins. That's why we now carry the Assembled Adafruit Pi T-Cobbler Plus - Breakout + Cable for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
